# Fritzing sketch schematic (saved by Fritzing 0.9.3b)
circuit board: 3cm x 9.9cm
breadboards: 1

parts:
  NANO = Arduino Nano (Rev3.0)
  PT2257 = IC, DIP package, 8 pins [chip_label=IC]
  INPUT = Audio Jack (TRS) 3.5mm [package="4Ucon 08780 [THT]"]
  OUTPUT = Audio Jack (TRS) 3.5mm [package="4Ucon 08780 [THT]"]
  IR = TSOP312.., 314.. [package=THT]
  C1 = Electrolytic Capacitor [capacitance=1µF package="100 mil [THT, electrolytic]"]
  C2 = Electrolytic Capacitor [capacitance=1µF package="100 mil [THT, electrolytic]"]
  C3 = Electrolytic Capacitor [capacitance=1µF package="100 mil [THT, electrolytic]"]
  C4 = Electrolytic Capacitor [capacitance=1µF package="100 mil [THT, electrolytic]"]
  R1 = Resistor [tolerance=±5% resistance=4.7k package=THT]
  R2 = Resistor [tolerance=±5% resistance=4.7k package=THT]
  J1 = Power Jack [package=power_jack_slot]

nets:
  GND: NANO.GND, PT2257.pin3, INPUT.Sleeve, OUTPUT.Sleeve, IR.GND, J1.GNDBREAK, J1.GND
  N1: NANO.D10, IR.Data
  N2: NANO.VIN, J1.PWR
  N3: NANO.5V, PT2257.pin6, IR.Vs, R1.Pin_1, R2.Pin_1
  N4: NANO.A5, PT2257.pin5, R1.Pin_0
  N5: NANO.A4, PT2257.pin4, R2.Pin_0
  N6: PT2257.pin1, C3.-
  N7: PT2257.pin2, C4.-
  N8: PT2257.pin7, C1.-
  N9: PT2257.pin8, C2.-
  N10: INPUT.Ring, C3.+
  N11: INPUT.Tip, C2.+
  N12: OUTPUT.Ring, C4.+
  N13: OUTPUT.Tip, C1.+

notes:
  INPUT
  OUTPUT
  R
  L
  POWER IN
